# Fritzing sketch MQTT_relay (saved by Fritzing 0.9.10b)
breadboards: 1

parts:
  Mod1 = KY-019 5V Relay Module [package="Breakout board"]
  F1 = Fan - Ventilador [package=THT]
  VCC1 = Battery
  M1 = DOIT Esp32 DevKit v1 (30 pins long, 11 pins width) [part_number=ESP32S-PIN30]

nets:
  N1: Mod1.S, M1.D4
  N2: Mod1.+, M1.3V3
  N3: Mod1.-, M1.GND
  N4: Mod1.Common, F1.5V
  N5: Mod1.NO, VCC1.+
  N6: F1.GND, VCC1.-

custom parts:
  KY-019 5V Relay Module: KY-019 5V Relay module, used to control AC circuits. (Special thanks to vanepp for fixing the PCB holes and other errors)
  Fan - Ventilador: Ventilador de 2 pines, se encuentra comunmente en computadoras de escritorio
  DOIT Esp32 DevKit v1 (30 pins long, 11 pins width): The DOIT Esp32 DevKit v1 is one of the development board created by DOIT to evaluate the ESP-WROOM-32 module. It is based on the ESP32 microcontroller that boasts Wifi, Bluetooth, Ethernet and Low Power support all in a single chip. (vanepp) made breadboard work, adjusted pin numbering and labels and reduced size of schematic and cleaned up pcb. This chip is 30pins long (2 x15) and 11 pins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
