# Fritzing sketch MQTT_scent (saved by Fritzing 0.9.10b)
breadboards: 1

parts:
  M2 = DOIT Esp32 DevKit v1 (30 pins long, 11 pins width) [part_number=ESP32S-PIN30]
  Mod3 = KY-019 5V Relay Module [package="Breakout board"]
  Mod4 = KY-019 5V Relay Module [package="Breakout board"]

nets:
  N1: M2.3V3, Mod3.+, Mod4.+
  N2: M2.GND, Mod3.-, Mod4.-
  N3: M2.D4, Mod3.S
  N4: M2.D5, Mod4.S

notes:
  USB Cable. Power for diffuser
  To diffuser button

custom parts:
  DOIT Esp32 DevKit v1 (30 pins long, 11 pins width): The DOIT Esp32 DevKit v1 is one of the development board created by DOIT to evaluate the ESP-WROOM-32 module. It is based on the ESP32 microcontroller that boasts Wifi, Bluetooth, Ethernet and Low Power support all in a single chip. (vanepp) made breadboard work, adjusted pin numbering and labels and reduced size of schematic and cleaned up pcb. This chip is 30pins long (2 x15) and 11 pins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
  KY-019 5V Relay Module: KY-019 5V Relay module, used to control AC circuits. (Special thanks to vanepp for fixing the PCB holes and other errors)
